# Fritzing sketch SQR_FG_Test (saved by Fritzing 0.9.2b)
breadboards: 2

parts:
  U1 = atmega328 [package=dip]
  XTAL1 = Crystal [frequency="16 Mhz" package=THT]
  C1 = Ceramic Capacitor [capacitance=100nF package="100 mil [THT, multilayer]"]
  C2 = Ceramic Capacitor [capacitance=100nF package="100 mil [THT, multilayer]"]
  C3 = Ceramic Capacitor [capacitance=100nF package="100 mil [THT, multilayer]"]
  R1 = Resistor [tolerance=±5% resistance=10k package=THT]
  R2 = Rotary Potentiometer (Small) [maximum_resistance=100kΩ package=THT]
  U2 = mystery part, 9 pins [chip_label="I2C LCD"]
  R3 = Resistor [tolerance=±5% resistance=22k package=THT]
  R4 = Resistor [tolerance=±5% resistance=12k package=THT]
  S1 = Pushbutton [package=THT]
  R5 = Rotary Potentiometer (Small) [maximum_resistance=100kΩ package=THT]
  IC1 = Dual Op-Amp [package=dip08]
  R6 = Resistor [tolerance=±5% resistance=10k package=THT]
  R7 = Resistor [tolerance=±5% resistance=10k package=THT]
  U3 = mystery part, 5 pins [chip_label=TLV1117-33]
  C5 = Ceramic Capacitor [capacitance=100nF package="100 mil [THT, multilayer]"]
  C6 = Ceramic Capacitor [capacitance=100nF package="100 mil [THT, multilayer]"]
  C7 = Electrolytic Capacitor [capacitance=1µF package="100 mil [THT, electrolytic]"]
  J2 = female pin header, 1 pin [form="♀ (female)"]
  RE1 = Rotary Encoder [package=THT]
  C8 = Ceramic Capacitor [capacitance=100nF package="100 mil [THT, multilayer]"]
  R8 = Resistor [tolerance=±5% resistance=33k package=THT]
  C9 = Electrolytic Capacitor [capacitance=1µF package="100 mil [THT, electrolytic]"]
  C10 = Electrolytic Capacitor [capacitance=1µF package="100 mil [THT, electrolytic]"]
  Q4 = Basic FET N-Channel [package="TO220 [THT]"]
  Q3 = Basic FET N-Channel [package="TO220 [THT]"]
  R9 = Resistor [tolerance=±5% resistance=10k package=THT]
  R10 = Resistor [tolerance=±5% resistance=10k package=THT]
  LED1 = LED - 5mm [color="Yellow (595nm)" package="5 mm [THT]"]
  LED2 = LED - 5mm [color="Green (570nm)" package="5 mm [THT]"]

nets:
  N1: U1.RESET, R1.Pin_0
  N2: U1.D0_(RX), RE1.EncoderPinB
  N3: U1.D1_(TX), RE1.EncoderPinA
  N4: U1.D2, S1.leg1
  N5: U1.VCC, U1.AVCC, U1.AREF, C3.0, R1.Pin_1, R2.leg1, IC1.A_V+, R6.Pin_0, U3.pin5, C5.0, C9.+
  N6: U1.GND#7, C1.1, C2.1, C3.1, R2.leg2, U2.pin6, R3.Pin_0, S1.leg0, IC1.A_V-, R7.Pin_1, U3.pin1, C5.1, C6.0, C7.-, RE1.EncoderPinC, C8.1, C10.-, Q4.source, LED1.cathode, LED2.cathode
  N7: U1.XLAT1, XTAL1.pin_0, C1.0
  N8: U1.XLAT2, XTAL1.pin_1, C2.0
  N9: U1.D10_(PWM), R8.Pin_0
  N10: U1.D11_(PWM), Q4.gate, R10.Pin_0
  N11: U1.D12, Q3.gate, R9.Pin_1
  N12: U1.A0, R2.wiper
  N13: U1.A3, R4.Pin_1
  N14: U1.A4, U2.pin5
  N15: U1.A5, U2.pin4
  N16: U2.pin3, R3.Pin_1, R4.Pin_0
  N17: U2.pin9, U3.pin3, C6.1, C7.+
  N18: R5.leg1, Q4.drain, Q3.drain
  N19: R5.wiper, IC1.A_+IN, C8.0
  N20: R5.leg2, R8.Pin_1
  N21: IC1.A_OUT, IC1.A_-IN, J2.pin1
  N22: IC1.B_+IN, R6.Pin_1, R7.Pin_0, C9.-, C10.+
  N23: IC1.B_-IN, IC1.B_OUT, Q3.source
  N24: R9.Pin_0, LED1.anode
  N25: R10.Pin_1, LED2.anode

notes:
  0V
  +3.3V
  0V
  +2.5V
  0V
  +5V
